# Fritzing sketch LEDCostume (saved by Fritzing 0.9.3b)
breadboards: 1

parts:
  U1 = ESP32S-HiLetgo [part_number=ESP32S-HiLetgo]
  Capacitor = Electrolytic Capacitor [capacitance=680µF voltage=25V part_number=VHT680M25-2 package="200 mil [THT, electrolytic]"]
  Power_USB = USB Connectors [package=s4b-ph]
  LLeg_USB = USB Connectors [package=s4b-ph]
  LLeg_Resistor = Resistor [tolerance=±5% resistance=330 package=THT]
  Shirt_Resistor = Resistor [tolerance=±5% resistance=330 package=THT]
  RLeg_Resistor = Resistor [tolerance=±5% resistance=330 package=THT]
  RLeg_USB = USB Connectors [package=s4b-ph]
  Shirt_USB = USB Connectors [package=s4b-ph]
  KEYPAD1 = Membrane Matrix Keypad
  RLeg_75_LEDs = WS2812 RGB LED strip
  Shirt_150_LEDs = WS2812 RGB LED strip
  LLeg_75_LEDs = WS2812 RGB LED strip
  PowerJuice = Battery Holders [package=battery-aa]

nets:
  N1: U1.GPIO32, KEYPAD1.7
  N2: U1.GPIO33, KEYPAD1.6
  N3: U1.GPIO25, KEYPAD1.5
  N4: U1.GPIO26, KEYPAD1.4
  N5: U1.GPIO27, KEYPAD1.3
  N6: U1.GPIO14, KEYPAD1.2
  N7: U1.GPIO12, KEYPAD1.1
  GND: U1.GND, Capacitor.-, Power_USB.GND, LLeg_USB.GND, RLeg_USB.GND, Shirt_USB.GND, RLeg_75_LEDs.GND, Shirt_150_LEDs.GND, LLeg_75_LEDs.GND, PowerJuice.-
  VCC: U1.VIN, Capacitor.+, Power_USB.D+, LLeg_USB.VBUS, RLeg_USB.VBUS, Shirt_USB.D-, Shirt_USB.VBUS, RLeg_75_LEDs.VCC, Shirt_150_LEDs.VCC, LLeg_75_LEDs.VCC, PowerJuice.+
  N8: U1.GPIO4, LLeg_Resistor.Pin_1
  N9: U1.GPIO16, Shirt_Resistor.Pin_1
  N10: U1.GPIO17, RLeg_Resistor.Pin_1
  N11: LLeg_USB.D+, LLeg_Resistor.Pin_0, LLeg_75_LEDs.DIN
  N12: Shirt_Resistor.Pin_0, Shirt_USB.D+, Shirt_150_LEDs.DIN
  N13: RLeg_Resistor.Pin_0, RLeg_USB.D+, RLeg_75_LEDs.DIN

custom parts:
  ESP32S-HiLetgo: HiLetgo ESP-WROOM-32 ESP32 ESP-32S Development Board 2.4GHz Dual-Mode WiFi + Bluetooth Dual Cores Microcontroller The ESP32 integrated with Antenna switches, RF Balun, power amplifiers, low-noise amplifiers, filters, and management modules, and the entire solution occupies the least area of PCB. 2.4 GHz Wi-Fi plus Bluetooth dual-mode chip, with TSMC Ultra-low power consumption 40nm technology,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
  Membrane Matrix Keypad: Membrane Matrix 3x4 Keypad
  WS2812 RGB LED strip: WS2812 strip
